// Logisim project BIP_Thaynara.circ as structural Verilog: 13 circuits, main circuit main
// MAIN
module main (
);

  wire CLEAR_ACC_out, CLEAR_PC_IR_ROM_out, CLEAR_RAM_out, Clock_out, controle_1_out_en_ram,
       controle_1_out_read_ram, controle_1_out_sel_op2, controle_1_out_sel_ula, controle_1_out_wr_acc,
       controle_1_out_wr_pc_en_rom_en_pc, controle_1_out_wr_ram;
  wire [1:0] controle_1_out_sel_op1;
  wire [11:0] adder_1_out, and_1_out, register_1_q;
  wire [15:0] ACC_q, bit_extender_1_out, IR_q, multiplexer_1_out, multiplexer_2_out, ram_1_data, rom_1_data,
       ua_1_out_ula;

  Clock Clock (.out(Clock_out));
  assign and_1_out = register_1_q & 12'hff;  // AND_Gate and_1, 12 bits wide
  Button CLEAR_PC_IR_ROM (.out(CLEAR_PC_IR_ROM_out));
  // Probe on ua_1_out_ula
  // Probe on register_1_q
  Register #(.width(12)) register_1 (
    .D(adder_1_out), .en(controle_1_out_wr_pc_en_rom_en_pc), .Q(register_1_q), .clk(Clock_out),
    .clr(CLEAR_PC_IR_ROM_out));
  Adder #(.width(12)) adder_1 (.a(and_1_out), .b(12'h1), .out(adder_1_out));  // open: cin, cout
  RAM #(.addrWidth(12), .dataWidth(16), .bus("separate")) ram_1 (
    .addr(IR_q[11:0]), .din(ua_1_out_ula), .data(ram_1_data), .str(controle_1_out_wr_ram),
    .sel(controle_1_out_en_ram), .clk(Clock_out), .clr(CLEAR_RAM_out));  // open: ld
  Button CLEAR_RAM (.out(CLEAR_RAM_out));
  // Probe on controle_1_out_sel_op2
  // Probe on multiplexer_1_out
  // Probe on rom_1_data
  // Probe on controle_1_out_sel_op1
  Multiplexer #(.width(16)) multiplexer_1 (
    .in0(ram_1_data), .in1(bit_extender_1_out), .out(multiplexer_1_out), .sel(controle_1_out_sel_op2));  // open: en
  ROM #(.addrWidth(12), .dataWidth(16)) rom_1 (.addr(register_1_q), .data(rom_1_data), .sel(1'b1));
  Register #(.width(16)) IR (.D(rom_1_data), .en(1'b1), .Q(IR_q), .clk(Clock_out), .clr(CLEAR_PC_IR_ROM_out));
  Multiplexer #(.select(2), .width(16)) multiplexer_2 (
    .in0(ram_1_data), .in1(bit_extender_1_out), .in2(ua_1_out_ula), .out(multiplexer_2_out),
    .sel(controle_1_out_sel_op1));  // open: in3, en
  UA ua_1 (.in_MUX(multiplexer_1_out), .in_ACC(ACC_q), .SEL_ULA(controle_1_out_sel_ula), .out_ULA(ua_1_out_ula));
  // Probe on IR_q[15:12]
  Register #(.width(16)) ACC (
    .D(multiplexer_2_out), .en(controle_1_out_wr_acc), .Q(ACC_q), .clk(Clock_out), .clr(CLEAR_ACC_out));
  Button CLEAR_ACC (.out(CLEAR_ACC_out));
  assign bit_extender_1_out = {{4{1'b0}}, IR_q[11:0]};  // Bit_Extender bit_extender_1
  // Probe on multiplexer_2_out
  // Probe on ACC_q
  // Probe on ua_1_out_ula
  // Probe on bit_extender_1_out
  Controle controle_1 (
    .C(IR_q[12]), .B(IR_q[13]), .A(IR_q[14]), .out_WR_PC_EN_ROM_EN_PC(controle_1_out_wr_pc_en_rom_en_pc),
    .out_WR_RAM(controle_1_out_wr_ram), .out_Read_RAM(controle_1_out_read_ram),
    .out_WR_ACC(controle_1_out_wr_acc), .out_EN_RAM(controle_1_out_en_ram),
    .out_Sel_Ula(controle_1_out_sel_ula), .out_Sel_OP2(controle_1_out_sel_op2),
    .out_SEL_OP1(controle_1_out_sel_op1));
  // Probe on controle_1_out_wr_pc_en_rom_en_pc
  // Probe on controle_1_out_wr_ram
  // Probe on controle_1_out_read_ram
  // Probe on controle_1_out_wr_acc
  // Probe on controle_1_out_sel_ula
  // Probe on controle_1_out_en_ram
  // Probe on controle_1_out_sel_op2
  // Probe on controle_1_out_sel_op1

  // Notes on the sheet:
  //   add_ram
  //   d_in
  //   WR_RAM
  //   Memória Dados
  //   DATAout
  //   Memória de Programa
  //   MUX_1
  //   dout
  //   contents of rom_1 (hex, n*v repeats v):
  //   3001 5002 1000 0 2000 5003 1001 0 3008 6000 1002 0 2002 7004 1003 0 2003 4002 1003
  //   MUX_2
  //   extensor
  //   ESSE NÃO TEM
endmodule

module UA (
  input  [15:0] in_MUX,
  input  [15:0] in_ACC,
  input  SEL_ULA,
  output [15:0] out_ULA
);

  wire [15:0] adder_1_out, demultiplexer_1_out0, demultiplexer_1_out1, demultiplexer_2_out0,
       demultiplexer_2_out1, subtractor_1_out;

  Demultiplexer #(.width(16)) demultiplexer_1 (
    .out0(demultiplexer_1_out0), .out1(demultiplexer_1_out1), .in(in_MUX), .sel(SEL_ULA));  // open: en
  Demultiplexer #(.width(16)) demultiplexer_2 (
    .out0(demultiplexer_2_out0), .out1(demultiplexer_2_out1), .in(in_ACC), .sel(SEL_ULA));  // open: en
  Adder #(.width(16)) adder_1 (
    .a(demultiplexer_1_out0), .b(demultiplexer_2_out0), .out(adder_1_out));  // open: cin, cout
  Subtractor #(.width(16)) subtractor_1 (
    .a(demultiplexer_1_out1), .b(demultiplexer_2_out1), .out(subtractor_1_out));  // open: bin, bout
  // Probe on adder_1_out
  // Probe on subtractor_1_out
  Multiplexer #(.width(16)) multiplexer_1 (
    .in0(adder_1_out), .in1(subtractor_1_out), .out(out_ULA), .sel(SEL_ULA));  // open: en

  // Notes on the sheet:
  //   Entrada_MUX
  //   Entrada_ACC
endmodule

module PC (
  input  EN_PC,
  input  CLOCK,
  output [11:0] out_PC_in_ADD_ROM
);

  wire button_1_out;
  wire [11:0] adder_1_out;
  wire [15:0] adder_2_out, and_1_out, register_1_q;

  Adder #(.width(12)) adder_1 (.a(12'h1), .b(out_PC_in_ADD_ROM), .out(adder_1_out));  // open: cin, cout
  // Probe on adder_1_out
  assign and_1_out = register_1_q & 16'hfff;  // AND_Gate and_1, 16 bits wide
  Counter #(.width(12), .max('hfff)) counter_1 (
    .load(EN_PC), .D(adder_1_out), .Q(out_PC_in_ADD_ROM), .clk(CLOCK), .clr(button_1_out));  // open: count, carry
  Adder #(.width(16)) adder_2 (.a(and_1_out), .b(16'h1), .out(adder_2_out));  // open: cin, cout
  Button button_1 (.out(button_1_out));
  Register #(.width(16)) register_1 (.D(adder_2_out), .Q(register_1_q));  // open: en, clk, clr
endmodule

// CONTROLE
module Controle (
  input  C,
  input  B,
  input  A,
  output out_WR_PC_EN_ROM_EN_PC,
  output out_WR_RAM,
  output out_Read_RAM,
  output out_WR_ACC,
  output out_EN_RAM,
  output out_Sel_Ula,
  output out_Sel_OP2,
  output [1:0] out_SEL_OP1
);

  wire SEL_OP1___bit_1_out_sel_op1_bit_1, SEL_OP1__bit_0_out_sel_op1_bit_0;

  EN_PC_WR_PC_EN_ROM EN_PC_WR_PC_EN_ROM (.C(C), .B(B), .A(A), .out_EN_PC_WR_PC(out_WR_PC_EN_ROM_EN_PC));
  WR_RAM WR_RAM (.C(C), .B(B), .A(A), .out_WR_RAM(out_WR_RAM));
  Read_RAM Read_RAM (.C(C), .B(B), .A(A), .out_Read_RAM(out_Read_RAM));
  WR_ACC WR_ACC (.C(C), .B(B), .A(A), .out_WR_ACC(out_WR_ACC));
  EN_RAM EN_RAM (.C(C), .B(B), .A(A), .out_EN_RAM(out_EN_RAM));
  Sel_Ula Sel_Ula (.C(C), .B(B), .A(A), .out_Sel_Ula(out_Sel_Ula));
  Sel_OP2 Sel_OP2 (.C(C), .B(B), .A(A), .out_Sel_OP2(out_Sel_OP2));
  SEL_OP1__bit_0 SEL_OP1__bit_0 (.C(C), .B(B), .A(A), .out_Sel_OP1_bit_0(SEL_OP1__bit_0_out_sel_op1_bit_0));
  Sel_OP1__bit_1 SEL_OP1___bit_1 (.C(C), .B(B), .A(A), .out_Sel_OP1_bit_1(SEL_OP1___bit_1_out_sel_op1_bit_1));
  // Probe on SEL_OP1__bit_0_out_sel_op1_bit_0
  // Probe on SEL_OP1___bit_1_out_sel_op1_bit_1
  assign out_SEL_OP1 = {{1{SEL_OP1___bit_1_out_sel_op1_bit_1}}, SEL_OP1__bit_0_out_sel_op1_bit_0};  // Bit_Extender bit_extender_1
  // Probe on out_SEL_OP1
endmodule

module EN_PC_WR_PC_EN_ROM (
  input  C,
  input  B,
  input  A,
  output out_EN_PC_WR_PC
);

  wire and_1_out, and_2_out, and_3_out, and_4_out, and_5_out, and_6_out, and_7_out, not_1_out, not_2_out,
       not_3_out;

  not not_1 (not_1_out, C);
  not not_2 (not_2_out, A);
  not not_3 (not_3_out, B);
  and and_1 (and_1_out, not_2_out, not_3_out, C);
  and and_2 (and_2_out, not_2_out, B, not_1_out);
  and and_3 (and_3_out, not_2_out, B, C);
  and and_4 (and_4_out, A, not_3_out, not_1_out);
  and and_5 (and_5_out, A, not_3_out, C);
  and and_6 (and_6_out, A, B, not_1_out);
  and and_7 (and_7_out, A, B, C);
  or or_1 (out_EN_PC_WR_PC, and_1_out, and_2_out, and_3_out, and_4_out, and_5_out, and_6_out, and_7_out);
endmodule

module WR_RAM (
  input  C,
  input  B,
  input  A,
  output out_WR_RAM
);

  wire not_1_out, not_2_out, not_3_out;

  not not_1 (not_1_out, C);
  not not_2 (not_2_out, A);
  not not_3 (not_3_out, B);
  and and_1 (out_WR_RAM, not_2_out, not_3_out, C);
endmodule

module Read_RAM (
  input  C,
  input  B,
  input  A,
  output out_Read_RAM
);

  wire and_1_out, and_2_out, and_3_out, and_4_out, and_5_out, not_1_out, not_2_out, not_3_out;

  not not_1 (not_1_out, C);
  not not_2 (not_2_out, B);
  not not_3 (not_3_out, A);
  and and_1 (and_1_out, not_3_out, B, not_1_out);
  and and_2 (and_2_out, not_3_out, B, C);
  and and_3 (and_3_out, A, not_2_out, C);
  and and_4 (and_4_out, A, B, not_1_out);
  and and_5 (and_5_out, A, B, C);
  or or_1 (out_Read_RAM, and_1_out, and_2_out, and_3_out, and_4_out, and_5_out);
endmodule

module WR_ACC (
  input  C,
  input  B,
  input  A,
  output out_WR_ACC
);

  wire and_1_out, and_2_out, and_3_out, and_4_out, and_5_out, and_6_out;

  and and_1 (and_1_out, ~A, B, ~C);  // AND_Gate
  and and_2 (and_2_out, ~A, B, C);  // AND_Gate
  and and_3 (and_3_out, A, ~B, ~C);  // AND_Gate
  and and_4 (and_4_out, A, ~B, C);  // AND_Gate
  and and_5 (and_5_out, A, B, ~C);  // AND_Gate
  and and_6 (and_6_out, A, B, C);
  or or_1 (out_WR_ACC, and_1_out, and_2_out, and_3_out, and_4_out, and_5_out, and_6_out);
endmodule

module EN_RAM (
  input  C,
  input  B,
  input  A,
  output out_EN_RAM
);

  wire and_1_out, and_2_out, and_3_out, and_4_out, not_1_out, not_2_out, not_3_out;

  not not_1 (not_1_out, C);
  not not_2 (not_2_out, A);
  not not_3 (not_3_out, B);
  and and_1 (and_1_out, not_2_out, not_3_out, C);
  and and_2 (and_2_out, not_2_out, B, not_1_out);
  and and_3 (and_3_out, A, not_3_out, not_1_out);
  and and_4 (and_4_out, A, B, not_1_out);
  or or_1 (out_EN_RAM, and_1_out, and_2_out, and_3_out, and_4_out);
endmodule

module Sel_Ula (
  input  C,
  input  B,
  input  A,
  output out_Sel_Ula
);

  wire and_1_out, and_2_out, not_1_out, not_2_out, not_3_out;

  not not_1 (not_1_out, C);
  not not_2 (not_2_out, A);
  not not_3 (not_3_out, B);
  and and_1 (and_1_out, A, B, not_1_out);
  and and_2 (and_2_out, A, B, C);
  or or_1 (out_Sel_Ula, and_1_out, and_2_out);
endmodule

module Sel_OP2 (
  input  C,
  input  B,
  input  A,
  output out_Sel_OP2
);

  wire and_1_out, and_2_out, and_3_out;

  and and_1 (and_1_out, ~A, B, C);  // AND_Gate
  and and_2 (and_2_out, A, ~B, C);  // AND_Gate
  and and_3 (and_3_out, A, B, C);
  or or_1 (out_Sel_OP2, and_1_out, and_2_out, and_3_out);
endmodule

module SEL_OP1__bit_0 (
  input  C,
  input  B,
  input  A,
  output out_Sel_OP1_bit_0
);

  and and_1 (out_Sel_OP1_bit_0, ~A, B, C);  // AND_Gate
endmodule

module Sel_OP1__bit_1 (
  input  C,
  input  B,
  input  A,
  output out_Sel_OP1_bit_1
);

  wire and_1_out, and_2_out, and_3_out, and_4_out;

  and and_1 (and_1_out, A, ~B, ~C);  // AND_Gate
  and and_2 (and_2_out, A, ~B, C);  // AND_Gate
  and and_3 (and_3_out, A, B, ~C);  // AND_Gate
  and and_4 (and_4_out, A, B, C);
  or or_1 (out_Sel_OP1_bit_1, and_1_out, and_2_out, and_3_out, and_4_out);
endmodule
